// Logisim project ALU8.circ as structural Verilog: 10 circuits, main circuit main
module main (
  input  [7:0] A,
  input  [7:0] B,
  input  Cin,
  input  [3:0] Op,
  output Cout,
  output ZF,
  output SF,
  output OF,
  output [7:0] F
);

  ALU alu_1 (.A(A), .B(B), .Cin(Cin), .Cout(Cout), .ZF(ZF), .SF(SF), .OF(OF), .Op(Op), .F(F));
endmodule

module ALU (
  input  [7:0] A,
  input  [7:0] B,
  input  Cin,
  input  [3:0] Op,
  output Cout,
  output ZF,
  output SF,
  output OF,
  output [7:0] F
);

  // andl AND: pin names not known; wires that end beside it: B, A
  // xorl XOR: pin names not known; wires that end beside it: B, A
  // addl ADD: pin names not known; wires that end beside it: B, Cin, A
  subl SUB (.A(A), .B(B), .Cin(Cin));
  asrl SHIFT_RIGHT (.A(A), .B(B), .Cin(Cin));
  lsll SHIFT_LEFT (.A(A), .B(B), .Cin(Cin));
  Multiplexer #(.select(4), .enable("false")) multiplexer_1 (
    .out(F[0]), .sel(Op));  // open: in0, in1, in2, in3, in4, in5, in6, in7, in8, in9, in10, in11, in12, in13, in14, in15
  // Pins of 1 and 8 bits meet at F
endmodule

module andl (
  input  [7:0] A,
  input  [7:0] B,
  output Cout,
  output ZF,
  output SF,
  output OF
);
endmodule

module xorl (
  input  [7:0] A,
  input  [7:0] B,
  output Cout,
  output ZF,
  output SF,
  output OF
);
endmodule

module addl (
  input  [7:0] A,
  input  [7:0] B,
  input  Cin,
  output Cout,
  output ZF,
  output SF,
  output OF
);
endmodule

module subl (
  input  [7:0] A,
  input  [7:0] B,
  input  Cin
);
endmodule

module asrl (
  input  [7:0] A,
  input  [7:0] B,
  input  Cin
);
endmodule

module lsll (
  input  [7:0] A,
  input  [7:0] B,
  input  Cin
);
endmodule

module is0 (
  input  [7:0] in_1,
  output out_2
);


  assign in_1[6:0] = {7{in_1[7]}};
  assign out_2 = in_1[7];
endmodule

module isNeg (
  input  [7:0] in_1,
  output out_2
);


  assign out_2 = in_1[7];
endmodule
